# Fritzing sketch turret (saved by Fritzing 0.9.3b)
breadboards: 1

parts:
  J1 = Basic Servo
  Part1 = Arduino Uno (Rev3) - ICSP
  hc-sr2 = hc-sr04
  LED1 = RGB LED (com. cathode, rgb) [package="5 mm [THT]"]
  hc-sr3 = hc-sr04
  hc-sr4 = hc-sr04
  hc-sr5 = hc-sr04
  hc-sr6 = hc-sr04
  R1 = Resistor [tolerance=±5% resistance=220 package="0402 [SMD]"]
  R2 = Resistor [tolerance=±5% resistance=220 package="0402 [SMD]"]
  R3 = Resistor [tolerance=±5% resistance=220 package="0402 [SMD]"]

nets:
  GND: J1.gnd, Part1.GND, hc-sr2.GND, LED1.common_cathode, hc-sr3.GND, hc-sr4.GND, hc-sr5.GND, hc-sr6.GND
  VCC: J1.vcc, Part1.VIN
  N1: J1.pulse, Part1.D3_PWM
  N2: Part1.ICSP_MOSI, Part1.D11_PWM/MOSI, LED1.green_anode, R2.Pin_0, R2.Pin_1
  N3: Part1.D8, hc-sr2.Echo
  N4: Part1.D9_PWM, hc-sr6.Echo
  N5: Part1.D10_PWM/SS, LED1.red_anode, R1.Pin_0, R1.Pin_1
  N6: Part1.D12/MISO, LED1.blue_anode, R3.Pin_0, R3.Pin_1
  N7: Part1.D4, hc-sr2.Trig, hc-sr3.Trig, hc-sr4.Trig, hc-sr5.Trig, hc-sr6.Trig
  N8: Part1.D5_PWM, hc-sr5.Echo
  N9: Part1.D6_PWM, hc-sr3.Echo
  N10: Part1.D7, hc-sr4.Echo
  VCC_2: Part1.5V, hc-sr2.VCC, hc-sr3.VCC, hc-sr4.VCC, hc-sr5.VCC, hc-sr6.VCC
